# Fritzing sketch paste_dispenser (saved by Fritzing 0.9.3b)
breadboards: 1

parts:
  Part1 = Arduino Pro Mini v13
  Squix1 = OLED 0.91" 128x32 I2C SSD1306 (GND/VCC)
  S1 = Pushbutton [package="[SMD]"]
  S2 = Pushbutton [package="[THT]"]
  S3 = Pushbutton [package="[THT]"]
  S4 = Pushbutton [package="[THT]"]
  Part3 = FTDI Basic Programmer
  Part4 = Adafruit TB6612 DC and Stepper Motor Driver [part_number="Adafruit #2448"]
  S5 = Pushbutton [package="[THT]"]
  MOTOR1 = Adafruit Gear-Reduced Stepper Motor (small)

nets:
  N1: Part1.DTR, Part3.DTR
  N2: Part1.D0/TX, Part3.RXI
  N3: Part1.D1/RX, Part3.TXO
  VCC: Part1.VCC, Squix1.VCC, Part3.POWER, Part4.PWRIN, Part4.VCC
  GND: Part1.GND, Squix1.GND, S1.Pin_3, S1.Pin_4, S2.Pin_3, S2.Pin_4, S3.Pin_3, S3.Pin_4, S4.Pin_3, S4.Pin_4, Part3.CTS, Part3.GND, Part4.GND, S5.Pin_3, S5.Pin_4, MOTOR1.YELLOW
  N4: Part1.A4, Squix1.SCA
  N5: Part1.A5, Squix1.SCL
  N6: Part1.A3, Part4.AIN1
  N7: Part1.A2, Part4.AIN2
  N8: Part1.A1, Part4.BIN1
  N9: Part1.A0, Part4.BIN2
  N10: Part1.D10_PWM/SS, Part4.PWMB
  N11: Part1.D9_PWM, Part4.PWMA
  N12: Part1.D8, Part4.STBY
  N13: Part1.D7, S1.Pin_1, S1.Pin_2
  N14: Part1.D6_PWM, S2.Pin_1, S2.Pin_2
  N15: Part1.D5_PWM, S3.Pin_1, S3.Pin_2
  N16: Part1.D4, S4.Pin_1, S4.Pin_2
  N17: Part1.D2, S5.Pin_1, S5.Pin_2
  N18: Part4.MOTORA1, MOTOR1.BLUE
  N19: Part4.MOTORA2, MOTOR1.PINK
  N20: Part4.MOTORB2, MOTOR1.ORANGE
  N21: Part4.MOTORB1, MOTOR1.RED

notes:
  Pushbuttons:
  Push Fast Slow Pull Footswitch
  Solder Paste Dispenser w/
  LED on pin 13.
  In sketch:
  pins.h:
  kLedPin = 13
  breathingled.cpp:
  #define LED_PWM 0

custom parts:
  OLED 0.91" 128x32 I2C SSD1306 (GND/VCC): OLED 0.91" 128x32 I2C SSD1306 Pinout: GND/VCC/SCL/SDA
  Adafruit TB6612 DC and Stepper Motor Driver: Spin two DC motors, step one bi-polar or uni-polar stepper, or fire off two solenoids with 1.2A per channel using the TB6612. These are perhaps better known as "the drivers in our assembled Adafruit Motorshield or Motor HAT." We really like these dual H-bridges, so if you want to control motors without a shield or HAT these are easy to include on any solderless breadboard or perma-proto.
  Adafruit Gear-Reduced Stepper Motor (small): Adafruit gear-reduction stepper motor (small)
